# Fritzing sketch arduinoproto (saved by Fritzing 0.9.3b)
circuit board: 3.18619cm x 3.56307cm
breadboards: 2

parts:
  clock1 = Resonator [package=resonator-smd]
  C9 = Ceramic Capacitor [capacitance=0.1µF package="0805 [SMD, multilayer]"]
  R6 = Resistor [tolerance=±5% resistance=10k package="0805 [SMD]"]
  rst = SWITCH-MOMENTARY-2 [package=tactile-switch-1101ne]
  bus = RJ45 Jack [package=rj45-8]
  bus_2 = RJ45 Jack [package=rj45-8]
  i2c = female pin header, 2 pins [form="♀ (female)"]
  328 = ATmega328 [package=tqfp]
  max485 = RS485 [package=so08]
  C10 = Ceramic Capacitor [capacitance=0.1µF package="0805 [SMD, multilayer]"]
  prog = Header 6 [package=em406]
  A0_A1 = female pin header, 2 pins [form="♀ (female)"]
  C11 = Ceramic Capacitor [capacitance=10µF voltage=16V package="0805 [SMD, multilayer]"]
  LM1117 = Voltage Regulator LM1117 [package=sot223]
  pwr = smd LED [color="Blue (525nm)" package="0805 [SMD]"]
  D5-D10 = double row rounded female pin header, 6 pins [form="♀ (female rounded)"]
  D5-D10_2 = double row male pin header, 6 pins [form="♂ (male)"]

nets:
  N1: clock1.1, 328.PB6(XTAL1_TOSC1)
  GND: clock1.2, rst.2, bus.1, bus_2.1, 328.GND, 328.AGND, max485._RE, max485.GND, C10.1, prog.1, prog.2, C11.1
  N2: clock1.3, 328.PB7(XTAL2_TOSC2)
  N3: C9.0, prog.6
  N4: C9.1, R6.Pin_0, rst.1, 328.PC6(_RESET)
  VCC: R6.Pin_1, 328.VCC, 328.AVCC, max485.VCC, C10.0, prog.3, pwr.cathode
  N5: bus.2, bus_2.2, C11.0, LM1117.IN
  N6: bus.3, bus_2.3, max485.A
  N7: bus.4, bus_2.4, max485.B
  N8: i2c.pin1, 328.PC5(ADC5_SCL)
  N9: i2c.pin2, 328.PC4(ADC4_SDA)
  N10: 328.PD3(INT1), max485.DI
  N11: 328.PD4(XCK_T0), max485.DE
  N12: 328.PD5(T1), D5-D10.pin1, D5-D10_2.pin1
  N13: 328.PD6(AIN0), D5-D10.pin2, D5-D10_2.pin2
  N14: 328.PD7(AIN1), D5-D10.pin3, D5-D10_2.pin3
  N15: 328.PB0(ICP), D5-D10.pin4, D5-D10_2.pin4
  N16: 328.PB1(OC1A), D5-D10.pin5, D5-D10_2.pin5
  N17: 328.PB2(SS_OC1B), D5-D10.pin6, D5-D10_2.pin6
  N18: 328.PC2(ADC2), A0_A1.pin2
  N19: 328.PC3(ADC3), A0_A1.pin1
  N20: 328.PD0(RXD), prog.4
  N21: 328.PD1(TXD), prog.5
  N22: 328.PD2(INT0), max485.RO
  N23: LM1117.OUT, pwr.anode
