# Fritzing sketch arduinoproto2 (saved by Fritzing 0.9.3b)
breadboards: 1

parts:
  Atmega1 = ATmega328 [package=tqfp]
  Y1 = Resonator [package=resonator-smd]
  S2 = SWITCH-MOMENTARY-2 [package=tactile-switch-1101ne]
  R1 = Resistor [tolerance=±5% resistance=10k package="0805 [SMD]"]
  C2 = Ceramic Capacitor [capacitance=100nF package="0805 [SMD, multilayer]"]
  C1 = Ceramic Capacitor [capacitance=100nF package="0603 [SMD, multilayer]"]
  J1 = female pin header, 6 pins [form="♀ (female)"]

nets:
  N1: Atmega1.GND, Atmega1.AGND, Y1.2, S2.1, C1.0, J1.pin1, J1.pin2
  N2: Atmega1.VCC, Atmega1.AVCC, R1.Pin_0, J1.pin3
  N3: Atmega1.PB6(XTAL1_TOSC1), Y1.1
  N4: Atmega1.PB7(XTAL2_TOSC2), Y1.3
  N5: Atmega1.AREF, C1.1
  N6: Atmega1.PC6(_RESET), S2.2, R1.Pin_1, C2.1
  N7: Atmega1.PD0(RXD), J1.pin4
  N8: Atmega1.PD1(TXD), J1.pin5
  N9: C2.0, J1.pin6
