# Fritzing sketch arduinoproto_cordwood (saved by Fritzing 0.9.3b)
breadboards: 2

parts:
  clock1 = Resonator [package=resonator-smd]
  rst = SWITCH-MOMENTARY-2 [package=tactile-switch-1101ne]
  bus = RJ45 Jack [package=rj45-8]
  bus_2 = RJ45 Jack [package=rj45-8]
  i2c = female pin header, 2 pins [form="♀ (female)"]
  328 = ATmega328 [package=tqfp]
  max485 = RS485 [package=so08]
  prog = Header 6 [package=em406]
  A0_A1 = female pin header, 2 pins [form="♀ (female)"]
  LM1117 = Voltage Regulator LM1117 [package=sot223]
  pwr = smd LED [color="Blue (525nm)" package="0805 [SMD]"]
  D5-D10 = double row rounded female pin header, 6 pins [form="♀ (female rounded)"]
  C10 = Ceramic Capacitor [capacitance=0.1µF package="200 mil [THT, multilayer]"]
  C11 = Ceramic Capacitor [capacitance=10µF voltage=16V package="200 mil [THT, multilayer]"]
  trans = LED - 5mm [color="Red (633nm)" package="5 mm [THT]"]  # not connected
  trans2 = LED - 5mm [color="Red (633nm)" package="5 mm [THT]"]  # not connected
  R6 = Resistor [tolerance=±5% resistance=10k package=THT]
  C9 = Ceramic Capacitor [capacitance=0.1µF package="200 mil [THT, multilayer]"]

nets:
  N1: clock1.1, 328.PB6(XTAL1_TOSC1)
  GND: clock1.2, rst.2, bus.1, bus_2.1, 328.GND, 328.AGND, max485._RE, max485.GND, prog.1, prog.2, C10.1, C11.1
  N2: clock1.3, 328.PB7(XTAL2_TOSC2)
  N3: rst.1, 328.PC6(_RESET), R6.Pin_0, C9.1
  N4: bus.2, bus_2.2, LM1117.IN, C11.0
  N5: bus.3, bus_2.3, max485.A
  N6: bus.4, bus_2.4, max485.B
  N7: i2c.pin1, 328.PC5(ADC5_SCL)
  N8: i2c.pin2, 328.PC4(ADC4_SDA)
  N9: 328.PD3(INT1), max485.DI
  N10: 328.PD4(XCK_T0), max485.DE
  VCC: 328.VCC, 328.AVCC, max485.VCC, prog.3, pwr.cathode, C10.0, R6.Pin_1
  N11: 328.PD5(T1), D5-D10.pin1
  N12: 328.PD6(AIN0), D5-D10.pin2
  N13: 328.PD7(AIN1), D5-D10.pin3
  N14: 328.PB0(ICP), D5-D10.pin4
  N15: 328.PB1(OC1A), D5-D10.pin5
  N16: 328.PB2(SS_OC1B), D5-D10.pin6
  N17: 328.PC2(ADC2), A0_A1.pin2
  N18: 328.PC3(ADC3), A0_A1.pin1
  N19: 328.PD0(RXD), prog.4
  N20: 328.PD1(TXD), prog.5
  N21: 328.PD2(INT0), max485.RO
  N22: prog.6, C9.0
  N23: LM1117.OUT, pwr.anode
