# Fritzing sketch camdentoRJ45 (saved by Fritzing 0.9.3b)
circuit board: 9.94781cm x 3.94937cm
breadboards: 1

parts:
  A = RJ45 Jack [package=rj45-8]
  B = RJ45 Jack [package=rj45-8]
  C = RJ45 Jack [package=rj45-8]
  D = RJ45 Jack [package=rj45-8]
  E = RJ45 Jack [package=rj45-8]
  F = RJ45 Jack [package=rj45-8]
  VCC = Camdenboss CTB0158-3 [part_number=CTB0158-3 package=THT]
  GND = Camdenboss CTB0158-3 [part_number=CTB0158-3 package=THT]
  + = female pin header, 2 pins [form="♀ (female)"]
  +_2 = female pin header, 2 pins [form="♀ (female)"]
  +_3 = female pin header, 2 pins [form="♀ (female)"]
  R1 = Resistor [tolerance=±5% resistance=220 package="1206 [SMD]"]
  R2 = Resistor [tolerance=±5% resistance=220 package="1206 [SMD]"]
  R3 = Resistor [tolerance=±5% resistance=220 package="1206 [SMD]"]

nets:
  N1: A.1, B.1, VCC.pin3, R1.Pin_1
  N2: A.2, B.2, GND.pin3, +_2.pin1
  N3: C.1, D.1, VCC.pin2, R2.Pin_1
  N4: C.2, D.2, GND.pin2, +_3.pin1
  N5: E.1, F.1, VCC.pin1, R3.Pin_1
  N6: E.2, F.2, GND.pin1, +.pin1
  N7: +.pin2, R3.Pin_0
  N8: +_2.pin2, R1.Pin_0
  N9: +_3.pin2, R2.Pin_0
