# Fritzing sketch relaysketch (saved by Fritzing 0.9.3b)
circuit board: 3.88032cm x 4.00988cm
breadboards: 1

parts:
  Q1 = NPN-Transistor [package="SOT-23 [SMD]"]
  bus = RJ45 Jack [package=rj45-8]
  bus_2 = RJ45 Jack [package=rj45-8]
  1117 = Voltage Regulator LM1117 [package=sot223]
  Q2 = NPN-Transistor [package="SOT-23 [SMD]"]
  D1 = Diode [package=sod-323]
  R1 = Resistor [tolerance=±5% resistance=220 package="0805 [SMD]"]
  R2 = Resistor [tolerance=±5% resistance=220 package="0805 [SMD]"]
  led3 = ws2812b [package="smd 2812b"]
  R3 = Resistor [tolerance=±5% resistance=220 package="0805 [SMD]"]
  R4 = Resistor [tolerance=±5% resistance=220 package="0805 [SMD]"]
  ACS712 = MOSFET-NCHANNEL-SOIC8 [package=so08]
  J2 = female pin header, 2 pins [form="♀ (female)"]
  J3 = female pin header, 7 pins [form="♀ (female)"]
  term = Resistor [tolerance=±5% resistance=220 package="0805 [SMD]"]
  DS2Y-5-DC5V3 = DS2Y-5-DC5V [part_number=DS2Y-5-DC5V]
  C1 = Ceramic Capacitor [capacitance=100nF package="0805 [SMD, multilayer]"]
  C2 = Ceramic Capacitor [capacitance=100nF package="0805 [SMD, multilayer]"]
  C3 = Ceramic Capacitor [capacitance=100nF package="0805 [SMD, multilayer]"]
  R5 = Resistor [tolerance=±5% resistance=220 package="0805 [SMD]"]
  REV = smd LED [color="Red (633nm)" package="0805 [SMD]"]
  R6 = Resistor [tolerance=±5% resistance=220 package="0805 [SMD]"]
  ON = smd LED [color="Red (633nm)" package="0805 [SMD]"]
  R7 = Resistor [tolerance=±5% resistance=220 package="0805 [SMD]"]
  load = Header 2 [package=jst-2-pth]
  C_D = female pin header, 2 pins [form="♀ (female)"]
  J4 = female pin header, 2 pins [form="♀ (female)"]

nets:
  VDD: Q1.2, bus.2, bus_2.2, 1117.ADJ, 1117.OUT, Q2.2, D1.C, led3.VDD, led3.VSS, R3.Pin_0, R4.Pin_1, ACS712.D, J2.pin1, J2.pin2, J3.pin3, J3.pin5, DS2Y-5-DC5V3.1_+, C1.0, C1.1, C2.1, C3.0, C3.1, R5.Pin_0, R5.Pin_1, R6.Pin_0, R7.Pin_1
  N1: Q1.0, R1.Pin_0
  N2: Q1.1, DS2Y-5-DC5V3.6_N.C., DS2Y-5-DC5V3.9_N.O., ON.anode
  N3: bus.1, bus_2.1, 1117.IN, ACS712.S, ACS712.G, DS2Y-5-DC5V3.8_N.O., DS2Y-5-DC5V3.11_N.C., C2.0
  N4: bus.3, bus_2.3, J3.pin7, term.Pin_1
  N5: bus.4, bus_2.4, J3.pin6, term.Pin_0
  N6: bus.5, bus_2.5, C_D.pin2
  N7: bus.7, bus_2.7, C_D.pin1
  N8: Q2.0, R2.Pin_0
  N9: Q2.1, D1.A, DS2Y-5-DC5V3.16_-, REV.anode
  N10: R1.Pin_1, R3.Pin_1, J3.pin1
  N11: R2.Pin_1, R4.Pin_0, J3.pin2
  N12: led3.DIN, J3.pin4
  N13: DS2Y-5-DC5V3.4_COM, load.1, J4.pin1
  N14: DS2Y-5-DC5V3.13_COM, load.2, J4.pin2
  N15: REV.cathode, R6.Pin_1
  N16: ON.cathode, R7.Pin_0

notes:
  gnd
  5v
  npx
  A
  B
  ocf
  lss
  on
  rev

custom parts:
  DS2Y-5-DC5V: Panasonic DS2Y-5-DC5V Relay with 2 form C contact
