# Fritzing sketch relaysketchB (saved by Fritzing 0.9.3b)
circuit board: 3.59148cm x 4.00453cm
breadboards: 1

parts:
  U2 = RJ45 Jack [package=rj45-8]
  U1 = RJ45 Jack [package=rj45-8]
  IC1 = Voltage Regulator LM1117 [package=sot223]
  U3 = RS485 [package=so08]

nets:
  N1: U2.1, U2.2, U1.1, U1.2, IC1.IN
  N2: U2.3, U2.4, U1.3, U1.4, U3.GND
  N3: U2.5, U1.5
  N4: U2.6, U1.6
  N5: U2.7, U1.7
  N6: U2.8, U1.8
  N7: IC1.OUT, U3.VCC
